# Fritzing sketch ServoControl (saved by Fritzing 0.9.3b)
breadboards: 1

parts:
  Part1 = Arduino Due (Rev2b)
  Mask_servo = Basic Servo
  U1 = RELAY-SOLIDSTATE [package=relay-s108t02]
  Stim = BNC [package=bnc]
  Beep = BNC [package=bnc]
  VCC1 = Battery block 9V
  Main_servo = Basic Servo

nets:
  VCC: Part1.5V, Mask_servo.vcc, U1.-, Main_servo.vcc
  GND: Part1.GND, Mask_servo.gnd, Stim.GND, Main_servo.gnd
  N1: Part1.D9_PWM, Main_servo.pulse
  N2: Part1.D11_PWM, Mask_servo.pulse
  N3: Part1.D3_PWM, Stim.OUT
  N4: Part1.D4_PWM/SS1, U1.+
  N5: U1.T1, VCC1.+
  N6: U1.T2, Beep.OUT
  N7: Beep.GND, VCC1.-
